// Logisim project cpu.circ as structural Verilog
module main (
  input  [31:0] INSTRUCTION,
  input  CLOCK,
  output [31:0] PROGRAM_COUNTER,
  output [31:0] ra,
  output [31:0] sp,
  output [31:0] t0,
  output [31:0] t1,
  output [31:0] t2,
  output [31:0] s0,
  output [31:0] s1,
  output [31:0] a0
);

  wire DMEM_p1, DMEM_p3;
  wire [2:0] funct3;
  wire [6:0] funct7;
  wire [24:0] INSTRUCTION_STAGE2;
  wire [31:0] adder_1_out, alu_result, read_data1, read_data2;

  Adder #(.width(32)) adder_1 (.a(PROGRAM_COUNTER), .b(32'h4), .out(adder_1_out));  // open: cin, cout
  Register #(.width(32)) register_1 (
    .D(INSTRUCTION), .en(1'b1), .clk(CLOCK),
    .Q({funct7, INSTRUCTION_STAGE2[24:15], funct3, INSTRUCTION_STAGE2[11:0]}));  // open: clr
  Register #(.width(32)) PC (.D(adder_1_out), .clk(CLOCK), .Q(PROGRAM_COUNTER));  // open: en, clr
  controls contrl (.in_1({funct7, INSTRUCTION_STAGE2[24:15], funct3, INSTRUCTION_STAGE2[11:0]}));  // open: MemRW, RegWEn, MemToReg, ALUSrc, Branch, ALUOp0, ALUOp1
  immediate_generation imm_gen (.in_1({funct7, INSTRUCTION_STAGE2[24:15], funct3, INSTRUCTION_STAGE2[11:0]}));  // open: out_2
  alu Arithmetic_Logic_Unit (.A(read_data1), .Result(alu_result));  // open: ALUSel, B, out_5, out_6
  regfile_main RegFile (
    .rs2(INSTRUCTION_STAGE2[24:20]), .rd(INSTRUCTION_STAGE2[11:7]), .Read_Data_1(read_data1),
    .Read_Data_2(read_data2), .ra(ra), .sp(sp), .t0(t0), .t1(t1), .t2(t2), .s0(s0), .s1(s1), .a0(a0),
    .rs1(INSTRUCTION_STAGE2[19:15]), .clk(CLOCK));  // open: Write_Data, RegWEn
  // mem_main DMEM: pin names not known; wires that end beside it: DMEM_p1, DMEM_p1, DMEM_p3

  // Other names for the same wires on the sheet: clk = CLOCK; opcode[6:0] = INSTRUCTION_STAGE2[6:0];
  //   rd[4:0] = INSTRUCTION_STAGE2[11:7]; INSTRUCTION_STAGE2 (some bits) = {funct7, funct3};
  //   rs1[4:0] = INSTRUCTION_STAGE2[19:15]; rs2[4:0] = INSTRUCTION_STAGE2[24:20]

  // Notes on the sheet:
  //   Output
  //   IMEM (do **NOT** move this)
  //   Inputs
  //   It is OK to move the PC, RegFile, ALU, and MEM to wherever is most convenient for you when constructing your CPU, and to delete this text
  //   Inputs/Outputs for testing. Do **NOT** move these.
endmodule

module instruction_decoder (
  input  [31:0] in_1
);


  // Other names for the same wires on the sheet: INSTRUCTION[31:0] = in_1
endmodule

module controls (
  input  [31:0] in_1,
  output MemRW,
  output RegWEn,
  output MemToReg,
  output ALUSrc,
  output Branch,
  output ALUOp0,
  output ALUOp1
);

  wire bit0, bit1, bit2;

  Multiplexer #(.select(3), .enable("false")) multiplexer_1 (
    .in0(1'b0), .in1(1'b1), .in2(1'b0), .in3(1'b1), .in4(1'b0), .in5(1'b0), .in6(1'b0), .in7(1'b0),
    .out(MemRW), .sel({bit2, bit1, bit0}));
  Multiplexer #(.select(3), .enable("false")) multiplexer_2 (
    .in0(1'b0), .in1(1'b1), .in2(1'b1), .in3(1'b1), .in4(1'b1), .in5(1'b1), .in6(1'b1), .in7(1'b0),
    .out(ALUSrc), .sel({bit2, bit1, bit0}));
  Multiplexer #(.select(3), .enable("false")) multiplexer_3 (
    .in0(1'b1), .in1(1'b1), .in2(1'b1), .in3(1'b0), .in4(1'b0), .in5(1'b0), .in6(1'b0), .in7(1'b0),
    .out(RegWEn), .sel({bit2, bit1, bit0}));
  Multiplexer #(.select(3), .enable("false")) multiplexer_4 (
    .in0(1'b0), .in1(1'b0), .in2(1'b0), .in3(1'b0), .in4(1'b1), .in5(1'b1), .in6(1'b1), .in7(1'b0),
    .out(Branch), .sel({bit2, bit1, bit0}));
  OpcodeTo3BitControls opcodeto3bitcontrols_1 (.in_1(in_1[6:0]), .out_2(bit0), .out_3(bit1), .out_4(bit2));
  Multiplexer #(.select(3), .enable("false")) multiplexer_5 (
    .in0(1'b0), .in1(1'b0), .in2(1'b0), .in3(1'b1), .in4(1'b1), .in5(1'b1), .in6(1'b1), .in7(1'b0),
    .out(ALUOp1), .sel({bit2, bit1, bit0}));
  Multiplexer #(.select(3), .enable("false")) multiplexer_6 (
    .in0(1'b0), .in1(1'b1), .in2(1'b0), .in3(1'b0), .in4(1'b0), .in5(1'b0), .in6(1'b0), .in7(1'b0),
    .out(MemToReg), .sel({bit2, bit1, bit0}));
  Multiplexer #(.select(3), .enable("false")) multiplexer_7 (
    .in0(1'b0), .in1(1'b1), .in2(1'b1), .in3(1'b1), .in4(1'b0), .in5(1'b1), .in6(1'b1), .in7(1'b0),
    .out(ALUOp0), .sel({bit2, bit1, bit0}));

  // Other names for the same wires on the sheet: INSTRUCTION[31:0] = in_1; opcode[6:0] = in_1[6:0];
  //   rd[4:0] = in_1[11:7]; func3[2:0] = in_1[14:12]; rs1[4:0] = in_1[19:15]; imm[11:0] = in_1[31:20]
endmodule

module immediate_generation (
  input  [31:0] in_1,
  output [31:0] out_2
);

  wire bit0, bit1, bit2;
  wire [31:0] bit_extender_3_out, bit_extender_4_out, bit_extender_5_out, I_IMM, S_IMM, SB_IMM, U_IMM, UJ_IMM;

  assign I_IMM = {{20{in_1[31]}}, in_1[31:20]};  // Bit_Extender bit_extender_1
  assign S_IMM = {{20{in_1[31]}}, {in_1[31:25], in_1[11:7]}};  // Bit_Extender bit_extender_2
  assign bit_extender_3_out = {{12{in_1[31]}}, in_1[31:12]};  // Bit_Extender bit_extender_3
  assign bit_extender_4_out = {{20{in_1[31]}}, {in_1[31], in_1[7], in_1[30:25], in_1[11:8]}};  // Bit_Extender bit_extender_4
  Shifter #(.width(32)) shifter_1 (.in(bit_extender_3_out), .\dist (5'b01100), .out(U_IMM));
  assign bit_extender_5_out = {{12{in_1[31]}}, {in_1[31], in_1[19:12], in_1[20], in_1[30:21]}};  // Bit_Extender bit_extender_5
  Shifter #(.width(32)) shifter_2 (.in(bit_extender_4_out), .\dist (5'b00001), .out(SB_IMM));
  Shifter #(.width(32)) shifter_3 (.in(bit_extender_5_out), .\dist (5'b00001), .out(UJ_IMM));
  OpcodeTo3Bit opcodeto3bit_1 (.Opcode(in_1[6:0]), .Bit0(bit0), .Bit1(bit1), .Bit2(bit2));
  Multiplexer #(.select(3), .width(32), .enable("false")) multiplexer_1 (
    .in0({32{1'b0}}), .in1(I_IMM), .in2(S_IMM), .in3(SB_IMM), .in4(U_IMM), .in5(UJ_IMM), .in6({32{1'b0}}),
    .in7({32{1'b0}}), .out(out_2), .sel({bit2, bit1, bit0}));

  // Other names for the same wires on the sheet: INSTRUCTION[31:0] = in_1; rd[4:0] = in_1[11:7];
  //   imm[11:0] = in_1[31:20]; func3[2:0] = in_1[14:12]; rs1[4:0] = in_1[19:15]; opcode[6:0] = in_1[6:0]
endmodule

module OpcodeTo3Bit (
  input  [6:0] Opcode,
  output Bit0,
  output Bit1,
  output Bit2
);

  wire and_6_out, and_7_out, and_8_out, not_1_out, not_2_out, not_3_out, not_4_out, not_5_out, not_6_out, O1,
       O2, O3, O4, O5, O6;
  wire [6:0] xnor_1_out, xnor_2_out, xnor_3_out, xnor_4_out, xnor_5_out, xnor_6_out, xnor_7_out, xnor_8_out;

  assign xnor_1_out = ~(Opcode ^ 7'b0110011);  // XNOR_Gate xnor_1, 7 bits wide
  assign xnor_2_out = ~(Opcode ^ 7'b0100011);  // XNOR_Gate xnor_2, 7 bits wide
  assign xnor_3_out = ~(Opcode ^ 7'b1100011);  // XNOR_Gate xnor_3, 7 bits wide
  assign xnor_4_out = ~(Opcode ^ 7'b0110111);  // XNOR_Gate xnor_4, 7 bits wide
  assign xnor_5_out = ~(Opcode ^ 7'b1101111);  // XNOR_Gate xnor_5, 7 bits wide
  and and_1 (O4, xnor_3_out[0], xnor_3_out[1], xnor_3_out[2], xnor_3_out[3], xnor_3_out[4], xnor_3_out[5], xnor_3_out[6]);
  and and_2 (O5, xnor_4_out[0], xnor_4_out[1], xnor_4_out[2], xnor_4_out[3], xnor_4_out[4], xnor_4_out[5], xnor_4_out[6]);
  and and_3 (O6, xnor_5_out[0], xnor_5_out[1], xnor_5_out[2], xnor_5_out[3], xnor_5_out[4], xnor_5_out[5], xnor_5_out[6]);
  and and_4 (O1, xnor_1_out[0], xnor_1_out[1], xnor_1_out[2], xnor_1_out[3], xnor_1_out[4], xnor_1_out[5], xnor_1_out[6]);
  assign xnor_6_out = ~(Opcode ^ 7'b0000011);  // XNOR_Gate xnor_6, 7 bits wide
  assign xnor_7_out = ~(Opcode ^ 7'b0010011);  // XNOR_Gate xnor_7, 7 bits wide
  assign xnor_8_out = ~(Opcode ^ 7'b1100111);  // XNOR_Gate xnor_8, 7 bits wide
  and and_5 (O3, xnor_2_out[0], xnor_2_out[1], xnor_2_out[2], xnor_2_out[3], xnor_2_out[4], xnor_2_out[5], xnor_2_out[6]);
  and and_6 (and_6_out, xnor_6_out[0], xnor_6_out[1], xnor_6_out[2], xnor_6_out[3], xnor_6_out[4], xnor_6_out[5], xnor_6_out[6]);
  and and_7 (and_7_out, xnor_7_out[0], xnor_7_out[1], xnor_7_out[2], xnor_7_out[3], xnor_7_out[4], xnor_7_out[5], xnor_7_out[6]);
  and and_8 (and_8_out, xnor_8_out[0], xnor_8_out[1], xnor_8_out[2], xnor_8_out[3], xnor_8_out[4], xnor_8_out[5], xnor_8_out[6]);
  not not_1 (not_1_out, O1);
  not not_2 (not_2_out, O2);
  not not_3 (not_3_out, O3);
  not not_4 (not_4_out, O4);
  not not_5 (not_5_out, O5);
  not not_6 (not_6_out, O6);
  or or_1 (O2, and_6_out, and_7_out, and_8_out);
  or or_2 (Bit0, O2, O4, O6);
  or or_3 (Bit1, O3, O4);
  or or_4 (Bit2, O5, O6);
endmodule

module OpcodeTo3BitControls (
  input  [6:0] in_1,
  output out_2,
  output out_3,
  output out_4
);

  wire and_7_out, and_8_out, not_1_out, not_2_out, not_3_out, not_4_out, not_5_out, not_6_out, not_7_out, O1,
       O2, O3, O4, O5, O6, O7;
  wire [6:0] xnor_1_out, xnor_2_out, xnor_3_out, xnor_4_out, xnor_5_out, xnor_6_out, xnor_7_out, xnor_8_out;

  assign xnor_1_out = ~(in_1 ^ 7'b1100011);  // XNOR_Gate xnor_1, 7 bits wide
  assign xnor_2_out = ~(in_1 ^ 7'b0110111);  // XNOR_Gate xnor_2, 7 bits wide
  assign xnor_3_out = ~(in_1 ^ 7'b1101111);  // XNOR_Gate xnor_3, 7 bits wide
  assign xnor_4_out = ~(in_1 ^ 7'b0110011);  // XNOR_Gate xnor_4, 7 bits wide
  assign xnor_5_out = ~(in_1 ^ 7'b0100011);  // XNOR_Gate xnor_5, 7 bits wide
  and and_1 (O5, xnor_1_out[0], xnor_1_out[1], xnor_1_out[2], xnor_1_out[3], xnor_1_out[4], xnor_1_out[5], xnor_1_out[6]);
  and and_2 (O6, xnor_2_out[0], xnor_2_out[1], xnor_2_out[2], xnor_2_out[3], xnor_2_out[4], xnor_2_out[5], xnor_2_out[6]);
  and and_3 (O7, xnor_3_out[0], xnor_3_out[1], xnor_3_out[2], xnor_3_out[3], xnor_3_out[4], xnor_3_out[5], xnor_3_out[6]);
  and and_4 (O1, xnor_4_out[0], xnor_4_out[1], xnor_4_out[2], xnor_4_out[3], xnor_4_out[4], xnor_4_out[5], xnor_4_out[6]);
  assign xnor_6_out = ~(in_1 ^ 7'b0010011);  // XNOR_Gate xnor_6, 7 bits wide
  and and_5 (O4, xnor_5_out[0], xnor_5_out[1], xnor_5_out[2], xnor_5_out[3], xnor_5_out[4], xnor_5_out[5], xnor_5_out[6]);
  assign xnor_7_out = ~(in_1 ^ 7'b0000011);  // XNOR_Gate xnor_7, 7 bits wide
  assign xnor_8_out = ~(in_1 ^ 7'b1100111);  // XNOR_Gate xnor_8, 7 bits wide
  and and_6 (O2, xnor_7_out[0], xnor_7_out[1], xnor_7_out[2], xnor_7_out[3], xnor_7_out[4], xnor_7_out[5], xnor_7_out[6]);
  and and_7 (and_7_out, xnor_6_out[0], xnor_6_out[1], xnor_6_out[2], xnor_6_out[3], xnor_6_out[4], xnor_6_out[5], xnor_6_out[6]);
  and and_8 (and_8_out, xnor_8_out[0], xnor_8_out[1], xnor_8_out[2], xnor_8_out[3], xnor_8_out[4], xnor_8_out[5], xnor_8_out[6]);
  not not_1 (not_1_out, O1);
  not not_2 (not_2_out, O2);
  not not_3 (not_3_out, O3);
  not not_4 (not_4_out, O4);
  not not_5 (not_5_out, O5);
  not not_6 (not_6_out, O6);
  not not_7 (not_7_out, O7);
  or or_1 (O3, and_7_out, and_8_out);
  or or_2 (out_3, O3, O4, O7);
  or or_3 (out_2, O2, O4, O6);
  or or_4 (out_4, O5, O6, O7);

  // Other names for the same wires on the sheet: bit0 = out_2; bit1 = out_3; bit2 = out_4; opcode[6:0] = in_1
endmodule
