// Logisim project cpu.circ as structural Verilog: 1 circuit, main circuit main
module main (
  input  [31:0] INSTRUCTION,
  input  CLOCK,
  output [31:0] PROGRAM_COUNTER,
  output [31:0] ra,
  output [31:0] sp,
  output [31:0] t0,
  output [31:0] t1,
  output [31:0] t2,
  output [31:0] s0,
  output [31:0] s1,
  output [31:0] a0
);

  wire DMEM_p1, DMEM_p3;
  wire [2:0] func3;
  wire [11:0] imm;
  wire [19:0] INSTRUCTION_STAGE2;
  wire [31:0] adder_1_out, alu_result, bit_extender_1_out, read_data1, read_data2;

  Adder #(.width(32)) adder_1 (.a(PROGRAM_COUNTER), .b(32'h4), .out(adder_1_out));  // open: cin, cout
  Register #(.width(32)) register_1 (
    .D(INSTRUCTION), .en(1'b1), .clk(CLOCK),
    .Q({imm, INSTRUCTION_STAGE2[19:15], func3, INSTRUCTION_STAGE2[11:0]}));  // open: clr
  Register #(.width(32)) PC (.D(adder_1_out), .clk(CLOCK), .Q(PROGRAM_COUNTER));  // open: en, clr
  assign bit_extender_1_out = {{20{imm[11]}}, imm};  // Bit_Extender bit_extender_1
  alu Arithmetic_Logic_Unit (
    .ALUSel(4'b0000), .B(bit_extender_1_out), .A(read_data1), .Result(alu_result));  // open: out_5, out_6
  regfile_main RegFile (
    .rs2(INSTRUCTION_STAGE2[19:15]), .rd(INSTRUCTION_STAGE2[11:7]), .Read_Data_1(read_data1),
    .Read_Data_2(read_data2), .ra(ra), .sp(sp), .t0(t0), .t1(t1), .t2(t2), .s0(s0), .s1(s1), .a0(a0),
    .rs1(INSTRUCTION_STAGE2[19:15]), .Write_Data(alu_result), .RegWEn(1'b1), .clk(CLOCK));
  // mem_main DMEM: pin names not known; wires that end beside it: DMEM_p1, DMEM_p1, DMEM_p3

  // Other names for the same wires on the sheet: clk = CLOCK; opcode[6:0] = INSTRUCTION_STAGE2[6:0];
  //   rd[4:0] = INSTRUCTION_STAGE2[11:7]; INSTRUCTION_STAGE2 (some bits) = {imm, func3};
  //   rs1[4:0] = INSTRUCTION_STAGE2[19:15]

  // Notes on the sheet:
  //   Output
  //   IMEM (do **NOT** move this)
  //   Inputs
  //   It is OK to move the PC, RegFile, ALU, and MEM to wherever is most convenient for you when constructing your CPU, and to delete this text
  //   Inputs/Outputs for testing. Do **NOT** move these.
endmodule
