// Logisim project alu.circ as structural Verilog: 1 circuit, main circuit alu
module alu (
  input  [31:0] A,
  input  [31:0] B,
  input  [3:0] ALUSel,
  output [31:0] Result,
  output [31:0] out_5,
  output [31:0] out_6
);

  wire and_1_out, and_2_out, and_3_out, and_4_out, and_6_out, and_7_out, not_1_out, not_2_out, not_3_out,
       not_4_out, or_3_out, overflow0;
  wire [31:0] add0, and0, divu0, or0, remu0, sll0, slt0, sra0, srl0, sub0, xor0;

  not not_1 (not_1_out, B[31]);
  Subtractor #(.width(32)) subtractor_1 (.a(A), .b(B), .out(sub0));  // open: bin, bout
  not not_2 (not_2_out, sub0[31]);
  and and_1 (and_1_out, not_1_out, not_2_out);
  and and_2 (and_2_out, and_1_out, A[31]);
  Shifter #(.width(32), .shift("ar")) shifter_1 (.in(A), .\dist (B[4:0]), .out(sra0));
  Shifter #(.width(32)) shifter_2 (.in(A), .\dist (B[4:0]), .out(sll0));
  and and_3 (and_3_out, B[31], sub0[31]);
  not not_3 (not_3_out, A[31]);
  and and_4 (and_4_out, and_3_out, not_3_out);
  or or_1 (overflow0, and_4_out, and_2_out);
  not not_4 (not_4_out, overflow0);
  Adder #(.width(32)) adder_1 (.a(A), .b(B), .out(add0));  // open: cin, cout
  assign and0 = A & B;  // AND_Gate and_5, 32 bits wide
  assign or0 = A | B;  // OR_Gate or_2, 32 bits wide
  assign xor0 = A ^ B;  // XOR_Gate xor_1, 32 bits wide
  Shifter #(.width(32), .shift("lr")) shifter_3 (.in(A), .\dist (B[4:0]), .out(srl0));
  and and_6 (and_6_out, sub0[31], not_4_out);
  and and_7 (and_7_out, not_2_out, overflow0);
  or or_3 (or_3_out, and_6_out, and_7_out);
  assign slt0 = {{31{1'b0}}, or_3_out};  // Bit_Extender bit_extender_1
  Multiplier #(.width(32)) multiplier_1 (.a(A), .b(B), .out(out_5), .cout(out_6));  // open: cin
  Multiplexer #(.select(4), .width(32), .enable("false")) multiplexer_1 (
    .in0(add0), .in1(and0), .in2(or0), .in3(xor0), .in4(srl0), .in5(sra0), .in6(sll0), .in7(slt0),
    .in8(divu0), .in9(remu0), .in10(out_5), .in11(out_6), .in12(sub0), .in13(B), .in14(B), .in15(B),
    .out(Result), .sel(ALUSel));
  Divider #(.width(32)) divider_1 (.a(A), .b(B), .out(divu0), .rem(remu0));  // open: upper

  // Other names for the same wires on the sheet: bsel0[31:0] = B; mul0[31:0] = out_5; mulhu0[31:0] = out_6

  // Notes on the sheet:
  //   INPUTS to your circuit
  //   DON'T CHANGE THE LOCATIONS OF THE INPUTS AND OUTPUTS!
  //   OUTPUT from your circuit
endmodule
