// Logisim project regfile.circ as structural Verilog: 1 circuit, main circuit main
module main (
  input  [4:0] rs1,
  input  [4:0] rs2,
  input  [4:0] rd,
  input  [31:0] Write_Data,
  input  RegWEn,
  input  clk,
  output [31:0] ra,
  output [31:0] sp,
  output [31:0] t0,
  output [31:0] t1,
  output [31:0] t2,
  output [31:0] s0,
  output [31:0] s1,
  output [31:0] a0,
  output [31:0] Read_Data_1,
  output [31:0] Read_Data_2,
  output [31:0] out_17,
  output [4:0] out_18
);

  wire we0, we1, we2, we3, we4, we5, we6, we7, we8, write_en1;
  wire [31:0] demultiplexer_1_out12, x0_input, x0_output, x1_input, x2_input, x5_input, x6_input, x7_input,
       x8_input, x9_input, x10_input;

  Register #(.width(1)) we_reg (.D(RegWEn), .en(1'b1), .clk(clk), .Q(write_en1));  // open: clr
  Register #(.width(32)) wd_reg (.D(Write_Data), .en(1'b1), .clk(clk), .Q(out_17));  // open: clr
  Register #(.width(5)) write_reg_reg (.D(rd), .en(1'b1), .clk(clk), .Q(out_18));  // open: clr
  Register #(.width(32)) x0 (.D(x0_input), .en(1'b0), .clk(clk), .Q(x0_output));  // open: clr
  Multiplexer #(.select(5), .width(32), .enable("false")) multiplexer_1 (
    .in0(x0_output), .in1(ra), .in2(sp), .in5(t0), .in6(t1), .in7(t2), .in8(s0), .in9(s1), .in10(a0),
    .in11({32{1'b0}}), .in12({32{1'b0}}), .in13({32{1'b0}}), .in14({32{1'b0}}), .in15({32{1'b0}}),
    .in16({32{1'b0}}), .in17({32{1'b0}}), .in18({32{1'b0}}), .in19({32{1'b0}}), .in20({32{1'b0}}),
    .in21({32{1'b0}}), .in22({32{1'b0}}), .in23({32{1'b0}}), .in24({32{1'b0}}), .in25({32{1'b0}}),
    .in26({32{1'b0}}), .in27({32{1'b0}}), .in28({32{1'b0}}), .in29({32{1'b0}}), .in30({32{1'b0}}),
    .out(Read_Data_1), .sel(rs1));  // open: in3, in4, in31
  Multiplexer #(.select(5), .width(32), .enable("false")) multiplexer_2 (
    .in0(x0_output), .in1(ra), .in2(sp), .in5(t0), .in6(t1), .in7(t2), .in8(s0), .in9(s1), .in10(a0),
    .in11({32{1'b0}}), .in12({32{1'b0}}), .in13({32{1'b0}}), .in14({32{1'b0}}), .in15({32{1'b0}}),
    .in16({32{1'b0}}), .in17({32{1'b0}}), .in18({32{1'b0}}), .in19({32{1'b0}}), .in20({32{1'b0}}),
    .in21({32{1'b0}}), .in22({32{1'b0}}), .in23({32{1'b0}}), .in24({32{1'b0}}), .in25({32{1'b0}}),
    .in26({32{1'b0}}), .in27({32{1'b0}}), .in28({32{1'b0}}), .in29({32{1'b0}}), .in30({32{1'b0}}),
    .out(Read_Data_2), .sel(rs2));  // open: in3, in4, in31
  Register #(.width(32)) x7 (.D(x7_input), .en(we5), .clk(clk), .Q(t2));  // open: clr
  Register #(.width(32)) x1 (.D(x1_input), .en(we1), .clk(clk), .Q(ra));  // open: clr
  Demultiplexer #(.select(5), .width(32), .enable("false")) demultiplexer_1 (
    .out0(x0_input), .out1(x1_input), .out2(x2_input), .out5(x5_input), .out6(x6_input), .out7(x7_input),
    .out8(x8_input), .out9(x9_input), .out10(x10_input), .out12(demultiplexer_1_out12),
    .out13(demultiplexer_1_out12), .out14(demultiplexer_1_out12), .out15(demultiplexer_1_out12),
    .out16(demultiplexer_1_out12), .out17(demultiplexer_1_out12), .out18(demultiplexer_1_out12),
    .out19(demultiplexer_1_out12), .out20(demultiplexer_1_out12), .out21(demultiplexer_1_out12),
    .out22(demultiplexer_1_out12), .out23(demultiplexer_1_out12), .out24(demultiplexer_1_out12),
    .out25(demultiplexer_1_out12), .out26(demultiplexer_1_out12), .out27(demultiplexer_1_out12),
    .out28(demultiplexer_1_out12), .out29(demultiplexer_1_out12), .out30(demultiplexer_1_out12),
    .out31(demultiplexer_1_out12), .in(Write_Data), .sel(rd));  // open: out3, out4, out11
  Register #(.width(32)) x8 (.D(x8_input), .en(we6), .clk(clk), .Q(s0));  // open: clr
  Register #(.width(32)) x2 (.D(x2_input), .en(we2), .clk(clk), .Q(sp));  // open: clr
  Register #(.width(32)) x9 (.D(x9_input), .en(we7), .clk(clk), .Q(s1));  // open: clr
  Register #(.width(32)) x5 (.D(x5_input), .en(we3), .clk(clk), .Q(t0));  // open: clr
  Register #(.width(32)) x6 (.D(x6_input), .en(we4), .clk(clk), .Q(t1));  // open: clr
  Register #(.width(32)) x10 (.D(x10_input), .en(we8), .clk(clk), .Q(a0));  // open: clr
  Demultiplexer #(.select(5), .enable("false")) demultiplexer_2 (
    .out0(we0), .out1(we1), .out2(we2), .out5(we3), .out6(we4), .out7(we5), .out8(we6), .out9(we7),
    .out10(we8), .in(RegWEn), .sel(rd));  // open: out3, out4, out11, out12, out13, out14, out15, out16, out17, out18, out19, out20, out21, out22, out23, out24, out25, out26, out27, out28, out29, out30, out31
  // also tied to GND on the sheet: {demultiplexer_1_out12[0], demultiplexer_1_out12[1], demultiplexer_1_out12[2], demultiplexer_1_out12[3], demultiplexer_1_out12[4], demultiplexer_1_out12[5], demultiplexer_1_out12[6], demultiplexer_1_out12[7], demultiplexer_1_out12[8], demultiplexer_1_out12[9], demultiplexer_1_out12[10], demultiplexer_1_out12[11], demultiplexer_1_out12[12], demultiplexer_1_out12[13], demultiplexer_1_out12[14], demultiplexer_1_out12[15], demultiplexer_1_out12[16], demultiplexer_1_out12[17], demultiplexer_1_out12[18], demultiplexer_1_out12[19], demultiplexer_1_out12[20], demultiplexer_1_out12[21], demultiplexer_1_out12[22], demultiplexer_1_out12[23], demultiplexer_1_out12[24], demultiplexer_1_out12[25], demultiplexer_1_out12[26], demultiplexer_1_out12[27], demultiplexer_1_out12[28], demultiplexer_1_out12[29], demultiplexer_1_out12[30], demultiplexer_1_out12[31]}

  // Other names for the same wires on the sheet: read_data1[31:0] = Read_Data_1; read_data2[31:0] = Read_Data_2;
  //   read_reg1[4:0] = rs1; read_reg2[4:0] = rs2; write_data1[31:0] = out_17; write_en = RegWEn; write_reg[4:0] = rd;
  //   write_reg1[4:0] = out_18; x1_output[31:0] = ra; x2_output[31:0] = sp; x5_output[31:0] = t0;
  //   x6_output[31:0] = t1; x7_output[31:0] = t2; x8_output[31:0] = s0; x9_output[31:0] = s1; x10_output[31:0] = a0

  // Notes on the sheet:
  //   INPUTS to your circuit
  //   DON'T CHANGE THE LOCATIONS OF THE INPUTS AND OUTPUTS!
  //   These are DEBUG/TEST outputs from your circuit.
  //   OUTPUTS from your circuit
endmodule
